# Fritzing sketch Project2IRsensor Schematic (saved by Fritzing 0.9.3b)
breadboards: 1

parts:
  S1 = H-Bridge with L298N
  Part1 = Arduino Uno (Rev3)
  M1 = DC Motor
  M2 = DC Motor
  VCC1 = Battery block 9V
  IR1 = TSOP312.., 314.. [package=THT]

nets:
  12V: S1.12V, Part1.VIN, VCC1.+, IR1.Vs
  GND: S1.GND, Part1.GND, VCC1.-, IR1.GND
  5V: S1.5V, Part1.5V
  N1: S1.ENA, Part1.D5_PWM
  N2: S1.IN1, Part1.D3_PWM
  N3: S1.IN2, Part1.D7
  N4: S1.IN3, Part1.D9_PWM
  N5: S1.IN4, Part1.D4
  N6: S1.ENB, Part1.D6_PWM
  N7: S1.M1-01, M2.pin_1
  N8: S1.M1-02, M2.pin_2
  N9: S1.M2-01, M1.pin_2
  N10: S1.M2-02, M1.pin_1
  N11: Part1.D2, IR1.Data

custom parts:
  H-Bridge with L298N: h-bridge
